// Logisim project TRABALHO DE ARQUITETURA DE COMPUTADORES CC3MB.circ as structural Verilog: 8 circuits, main circuit main
module main (
  input  [3:0] B,
  input  [3:0] A,
  input  [2:0] \Operações ,
  output Overflow,
  output Overflow_2,
  output [3:0] S
);

  wire decoder_1_s0, decoder_1_s1, decoder_1_s2, decoder_1_s4;
  wire [3:0] add_4_1_out_5, sub_4_1_out_5;

  Decoder decoder_1 (
    .in_1(\Operações ), .S0(decoder_1_s0), .S1(decoder_1_s1), .S2(decoder_1_s2), .S4(decoder_1_s4));  // open: S3, S5, S6, S7
  Buffer buffer_1 (.B(B), .Controle(decoder_1_s0), .S(S));
  ADD_4 add_4_1 (.in_1(A), .VAI_1(Overflow), .in_2(B), .VEM_1(1'b0), .out_5(add_4_1_out_5));
  Buffer buffer_2 (.B(add_4_1_out_5), .Controle(decoder_1_s1), .S(S));
  Sub_4 sub_4_1 (.Overflow(Overflow_2), .in_1(A), .in_2(B), .Vem_1(1'b0), .out_5(sub_4_1_out_5));
  Buffer buffer_3 (.B(sub_4_1_out_5), .Controle(decoder_1_s2), .S(S));
  Buffer_invertido buffer_invertido_1 (.in_1(B), .in_2(decoder_1_s4), .out_3(S));
endmodule

module ADD_1 (
  input  A,
  input  B,
  input  VEM_1,
  output S,
  output VAI_1
);

  wire and_1_out, and_2_out, or_1_out, xor_1_out;

  xor xor_1 (xor_1_out, A, B);
  or or_1 (or_1_out, B, VEM_1);
  and and_1 (and_1_out, B, VEM_1);
  xor xor_2 (S, xor_1_out, VEM_1);
  and and_2 (and_2_out, or_1_out, A);
  or or_2 (VAI_1, and_2_out, and_1_out);
endmodule

module ADD_4 (
  input  [3:0] in_1,
  input  [3:0] in_2,
  input  VEM_1,
  output VAI_1,
  output [3:0] out_5
);

  wire add_1_2_vai_1, add_1_3_vai_1, add_1_4_vai_1;

  ADD_1 add_1_1 (.A(in_1[3]), .B(in_2[3]), .VEM_1(add_1_2_vai_1), .S(out_5[3]), .VAI_1(VAI_1));
  ADD_1 add_1_2 (.A(in_1[2]), .B(in_2[2]), .VEM_1(add_1_3_vai_1), .S(out_5[2]), .VAI_1(add_1_2_vai_1));
  ADD_1 add_1_3 (.A(in_1[1]), .B(in_2[1]), .VEM_1(add_1_4_vai_1), .S(out_5[1]), .VAI_1(add_1_3_vai_1));
  ADD_1 add_1_4 (.A(in_1[0]), .B(in_2[0]), .VEM_1(VEM_1), .S(out_5[0]), .VAI_1(add_1_4_vai_1));
endmodule

module Sub_1 (
  input  A,
  input  B,
  input  VEM_1,
  output S,
  output VAI_1
);

  wire and_1_out, and_2_out, not_1_out, or_1_out, xor_1_out;

  not not_1 (not_1_out, A);
  xor xor_1 (xor_1_out, A, B);
  or or_1 (or_1_out, B, VEM_1);
  and and_1 (and_1_out, B, VEM_1);
  xor xor_2 (S, xor_1_out, VEM_1);
  and and_2 (and_2_out, or_1_out, not_1_out);
  or or_2 (VAI_1, and_2_out, and_1_out);
endmodule

module Sub_4 (
  input  [3:0] in_1,
  input  [3:0] in_2,
  input  Vem_1,
  output Overflow,
  output [3:0] out_5
);

  wire sub_1_2_vai_1, sub_1_3_vai_1, sub_1_4_vai_1;

  Sub_1 sub_1_1 (.A(in_1[3]), .B(in_2[3]), .VEM_1(sub_1_2_vai_1), .S(out_5[3]), .VAI_1(Overflow));
  Sub_1 sub_1_2 (.A(in_1[2]), .B(in_2[2]), .VEM_1(sub_1_3_vai_1), .S(out_5[2]), .VAI_1(sub_1_2_vai_1));
  Sub_1 sub_1_3 (.A(in_1[1]), .B(in_2[1]), .VEM_1(sub_1_4_vai_1), .S(out_5[1]), .VAI_1(sub_1_3_vai_1));
  Sub_1 sub_1_4 (.A(in_1[0]), .B(in_2[0]), .VEM_1(Vem_1), .S(out_5[0]), .VAI_1(sub_1_4_vai_1));
endmodule

module Buffer (
  input  [3:0] B,
  input  Controle,
  output [3:0] S
);

  assign S[3] = Controle ? B[3] : 1'bz;  // Controlled_Buffer controlled_buffer_1
  assign S[2] = Controle ? B[2] : 1'bz;  // Controlled_Buffer controlled_buffer_2
  assign S[1] = Controle ? B[1] : 1'bz;  // Controlled_Buffer controlled_buffer_3
  assign S[0] = Controle ? B[0] : 1'bz;  // Controlled_Buffer controlled_buffer_4
endmodule

module Decoder (
  input  [2:0] in_1,
  output S0,
  output S1,
  output S2,
  output S3,
  output S4,
  output S5,
  output S6,
  output S7
);

  wire not_1_out, not_2_out, not_3_out, not_4_out, not_5_out, not_6_out, not_7_out, not_8_out, not_9_out,
       not_10_out, not_11_out, not_12_out;

  not not_1 (not_1_out, in_1[2]);
  and and_1 (S0, not_1_out, not_2_out, not_3_out);
  not not_2 (not_2_out, in_1[1]);
  not not_3 (not_3_out, in_1[0]);
  not not_4 (not_4_out, in_1[2]);
  and and_2 (S1, not_4_out, not_5_out, in_1[0]);
  not not_5 (not_5_out, in_1[1]);
  not not_6 (not_6_out, in_1[2]);
  and and_3 (S2, not_6_out, in_1[1], not_7_out);
  not not_7 (not_7_out, in_1[0]);
  not not_8 (not_8_out, in_1[2]);
  and and_4 (S3, not_8_out, in_1[1], in_1[0]);
  not not_9 (not_9_out, in_1[1]);
  and and_5 (S4, in_1[2], not_9_out, not_10_out);
  not not_10 (not_10_out, in_1[0]);
  not not_11 (not_11_out, in_1[1]);
  and and_6 (S5, in_1[2], not_11_out, in_1[0]);
  and and_7 (S6, in_1[2], in_1[1], not_12_out);
  not not_12 (not_12_out, in_1[0]);
  and and_8 (S7, in_1[2], in_1[1], in_1[0]);
endmodule

module Buffer_invertido (
  input  [3:0] in_1,
  input  in_2,
  output [3:0] out_3
);

  assign out_3[3] = in_2 ? ~in_1[3] : 1'bz;  // Controlled_Inverter controlled_inverter_1
  assign out_3[2] = in_2 ? ~in_1[2] : 1'bz;  // Controlled_Inverter controlled_inverter_2
  assign out_3[1] = in_2 ? ~in_1[1] : 1'bz;  // Controlled_Inverter controlled_inverter_3
  assign out_3[0] = in_2 ? ~in_1[0] : 1'bz;  // Controlled_Inverter controlled_inverter_4
endmodule
